// Logisim project PARTE_1_ULA.circ as structural Verilog
module HALFADDER (
  input  A,
  input  B,
  output S,
  output C0
);

  xor xor_1 (S, A, B);
  and and_1 (C0, A, B);
endmodule

module FULLADDER (
  input  Ci,
  input  A,
  input  B,
  output S,
  output C0
);

  wire halfadder_1_c0, halfadder_1_s, halfadder_2_c0;

  HALFADDER halfadder_1 (.A(A), .B(B), .S(halfadder_1_s), .C0(halfadder_1_c0));
  HALFADDER halfadder_2 (.A(Ci), .B(halfadder_1_s), .S(S), .C0(halfadder_2_c0));
  or or_1 (C0, halfadder_2_c0, halfadder_1_c0);
endmodule

module ADDER4B (
  input  C0,
  input  A0,
  input  B0,
  input  A1,
  input  B1,
  input  A2,
  input  B2,
  input  A3,
  input  B3,
  output S0,
  output S1,
  output S2,
  output S3,
  output C4
);

  wire fulladder_1_c0, fulladder_2_c0, fulladder_3_c0;

  FULLADDER fulladder_1 (.Ci(C0), .A(A0), .B(B0), .S(S0), .C0(fulladder_1_c0));
  FULLADDER fulladder_2 (.Ci(fulladder_1_c0), .A(A1), .B(B1), .S(S1), .C0(fulladder_2_c0));
  FULLADDER fulladder_3 (.Ci(fulladder_2_c0), .A(A2), .B(B2), .S(S2), .C0(fulladder_3_c0));
  FULLADDER fulladder_4 (.Ci(fulladder_3_c0), .A(A3), .B(B3), .S(S3), .C0(C4));
endmodule

module ADDER8B (
  input  c0,
  input  A0,
  input  B0,
  input  A1,
  input  B1,
  input  A2,
  input  B2,
  input  A3,
  input  B3,
  input  A4,
  input  B4,
  input  A5,
  input  B5,
  input  A6,
  input  B6,
  input  A7,
  input  B7,
  output S0,
  output S1,
  output S2,
  output S3,
  output S4,
  output S5,
  output S6,
  output S7,
  output C8
);

  wire adder4b_1_c4;

  ADDER4B adder4b_1 (
    .C0(c0), .A0(A0), .B0(B0), .A1(A1), .B1(B1), .A2(A2), .B2(B2), .A3(A3), .B3(B3), .S0(S0), .S1(S1),
    .S2(S2), .S3(S3), .C4(adder4b_1_c4));
  ADDER4B adder4b_2 (
    .C0(adder4b_1_c4), .A0(A4), .B0(B4), .A1(A5), .B1(B5), .A2(A6), .B2(B6), .A3(A7), .B3(B7), .S0(S4),
    .S1(S5), .S2(S6), .S3(S7), .C4(C8));
endmodule

module HALFSUB (
  input  A,
  input  B,
  output S,
  output t0
);

  xor xor_1 (S, A, B);
  and and_1 (t0, ~A, B);  // AND_Gate
endmodule

module FULLSUB (
  input  ti,
  input  A,
  input  B,
  output S,
  output t0
);

  wire halfsub_1_s, halfsub_1_t0, halfsub_2_t0;

  HALFSUB halfsub_1 (.A(A), .B(B), .S(halfsub_1_s), .t0(halfsub_1_t0));
  HALFSUB halfsub_2 (.A(ti), .B(halfsub_1_s), .S(S), .t0(halfsub_2_t0));
  or or_1 (t0, halfsub_2_t0, halfsub_1_t0);
endmodule

module SUB4B (
  input  Ti,
  input  A0,
  input  B0,
  input  A1,
  input  B1,
  input  A2,
  input  B2,
  input  A3,
  input  B3,
  output S0,
  output S1,
  output S2,
  output S3,
  output T4
);

  wire fullsub_1_t0, fullsub_2_t0, fullsub_3_t0;

  FULLSUB fullsub_1 (.ti(Ti), .A(A0), .B(B0), .S(S0), .t0(fullsub_1_t0));
  FULLSUB fullsub_2 (.ti(fullsub_1_t0), .A(A1), .B(B1), .S(S1), .t0(fullsub_2_t0));
  FULLSUB fullsub_3 (.ti(fullsub_2_t0), .A(A2), .B(B2), .S(S2), .t0(fullsub_3_t0));
  FULLSUB fullsub_4 (.ti(fullsub_3_t0), .A(A3), .B(B3), .S(S3), .t0(T4));
endmodule

module SUB8B (
  input  Ti,
  input  A0,
  input  B0,
  input  A1,
  input  B1,
  input  A2,
  input  B2,
  input  A3,
  input  B3,
  input  A4,
  input  B4,
  input  A5,
  input  B5,
  input  A6,
  input  B6,
  input  A7,
  input  B7,
  output S0,
  output S1,
  output S2,
  output S3,
  output S4,
  output S5,
  output S6,
  output S7,
  output T8
);

  wire sub4b_1_t4;

  SUB4B sub4b_1 (
    .Ti(Ti), .A0(A0), .B0(B0), .A1(A1), .B1(B1), .A2(A2), .B2(B2), .A3(A3), .B3(B3), .S0(S0), .S1(S1),
    .S2(S2), .S3(S3), .T4(sub4b_1_t4));
  SUB4B sub4b_2 (
    .Ti(sub4b_1_t4), .A0(A4), .B0(B4), .A1(A5), .B1(B5), .A2(A6), .B2(B6), .A3(A7), .B3(B7), .S0(S4),
    .S1(S5), .S2(S6), .S3(S7), .T4(T8));
endmodule

module DECODE3X8 (
  input  B2,
  input  B1,
  input  B0,
  output E0,
  output E1,
  output E2,
  output E3,
  output E4,
  output E5,
  output E6,
  output E7
);

  and and_1 (E0, ~B2, ~B1, ~B0);  // AND_Gate
  and and_2 (E1, ~B2, ~B1, B0);  // AND_Gate
  and and_3 (E2, ~B2, B1, ~B0);  // AND_Gate
  and and_4 (E3, ~B2, B1, B0);  // AND_Gate
  and and_5 (E4, B2, ~B1, ~B0);  // AND_Gate
  and and_6 (E5, B2, ~B1, B0);  // AND_Gate
  and and_7 (E6, B2, B1, ~B0);  // AND_Gate
  and and_8 (E7, B2, B1, B0);
endmodule

module UL (
  input  A,
  input  B,
  output S0,
  output S1,
  output S2,
  output S3,
  output S4,
  output S5
);

  wire xor_2_out;

  and and_1 (S0, A, B);
  or or_1 (S1, A, B);
  xor xor_1 (S2, A, B);
  nand nand_1 (S3, A, B);
  nor nor_1 (S4, A, B);
  xor xor_2 (xor_2_out, A, B);
  not not_1 (S5, xor_2_out);
endmodule
